# Fritzing sketch circuit (saved by Fritzing 1.0.8)
breadboards: 1

parts:
  Raspberry_Pi_1 = Raspberry Pi 3 [part_number=RPI-3-V1.2]
  S1 = Pushbutton [package=THT]
  S2 = Pushbutton [package=THT]
  S3 = Pushbutton [package=THT]
  S4 = Pushbutton [package=THT]
  S5 = Pushbutton [package=THT]  # not connected
  S6 = Pushbutton [package=THT]  # not connected
  S7 = Pushbutton [package=THT]  # not connected
  S8 = Pushbutton [package=THT]  # not connected
  LED1 = LED - 5mm [color="Red (633nm)" current=0.030A package="5 mm [THT]"]  # not connected
  LED2 = LED - 5mm [color="Red (633nm)" current=0.030A package="5 mm [THT]"]  # not connected
  LED3 = LED - 5mm [color="Red (633nm)" current=0.030A package="5 mm [THT]"]  # not connected
  LED4 = LED - 5mm [color="Red (633nm)" current=0.030A package="5 mm [THT]"]  # not connected
  LED5 = LED - 5mm [color="Green (560nm)" current=0.030A package="5 mm [THT]"]  # not connected
  R1 = Resistor [tolerance=±5% power=0.25W resistance=220 package=THT]  # not connected
  R2 = Resistor [tolerance=±5% power=0.25W resistance=220 package=THT]  # not connected
  R3 = Resistor [tolerance=±5% power=0.25W resistance=220 package=THT]  # not connected
  R4 = Resistor [tolerance=±5% power=0.25W resistance=220 package=THT]  # not connected
  R5 = Resistor [tolerance=±5% power=0.25W resistance=220 package=THT]  # not connected
  R6 = Resistor [tolerance=±5% power=0.25W resistance=10k package=THT]
  R7 = Resistor [tolerance=±5% power=0.25W resistance=10k package=THT]
  R8 = Resistor [tolerance=±5% power=0.25W resistance=10k package=THT]
  R9 = Resistor [tolerance=±5% power=0.25W resistance=10k package=THT]
  R10 = Resistor [tolerance=±5% power=0.25W resistance=10k package=THT]  # not connected
  R11 = Resistor [tolerance=±5% power=0.25W resistance=10k package=THT]  # not connected
  R12 = Resistor [tolerance=±5% power=0.25W resistance=10k package=THT]  # not connected
  R13 = Resistor [tolerance=±5% power=0.25W resistance=10k package=THT]  # not connected

nets:
  3V3: Raspberry_Pi_1.3v3, Raspberry_Pi_1.3V3, S1.leg1, S2.leg1, S3.leg1, S4.leg1, R6.Pin_1, R7.Pin_1, R8.Pin_1, R9.Pin_1
  N1: Raspberry_Pi_1.GPIO2, S1.leg0
  N2: Raspberry_Pi_1.GPIO3, S2.leg0
  N3: Raspberry_Pi_1.GIPO4, S3.leg0
  N4: Raspberry_Pi_1.GIPO17, S4.leg0
  N5: Raspberry_Pi_1.GND, R6.Pin_0, R7.Pin_0, R8.Pin_0, R9.Pin_0
